# Fritzing sketch Cloud Lamp (saved by Fritzing 0.8.7b)
breadboards: 1

parts:
  Eleman1 = Arduino Uno (Rev3)
  U1 = WS2812 RGB LED strip
  FC-1 = Sound Sensor

nets:
  N1: Eleman1.A0, FC-1.OUT
  N2: Eleman1.D7, U1.DOUT
  GND: Eleman1.GND, U1.GND, FC-1.GND
  VCC: Eleman1.VIN, U1.VCC, FC-1.VCC

custom parts:
  WS2812 RGB LED strip: WS2812 strip
